# Fritzing sketch schematic (saved by Fritzing 0.9.3b)
circuit board: 8.46667cm x 5.64444cm
breadboards: 1

parts:
  part = Arduino Pro Mini (3.3V)
  R1 = Resistor [tolerance=±5% resistance=1k package="2010 [SMD]"]
  part_2 = 24 NeoPixel Ring
  connection_to_pedal = Audio Jack Breakout

nets:
  VCC: part.VCC, R1.Pin_0, part_2.VDD
  GND: part.GND, part_2.GND, connection_to_pedal.GND
  N1: part.A0, R1.Pin_1, connection_to_pedal.RING
  N2: part.D6, part_2.IN

custom parts:
  24 NeoPixel Ring: 24 ultra bright smart LED NeoPixels are arranged in a circle with 2.6" (66mm) outer diameter. The rings are 'chainable' - connect the output pin of one to the input pin of another. Use only one microcontroller pin to control as many as you can chain together! Each LED is addressable as the driver chip is inside the LED. Each one has ~18mA constant current drive so the color will be very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
